# Fritzing sketch Schema (saved by Fritzing 0.9.2b)

parts:
  LED1 = DUO LED RG [package="5 mm [THT]"]
  Composant1 = Arduino Nano (Rev3.0) (ICSP)
  S1 = Momentary Switch [package=ksa_sealed_tac_switch]
  U2 = mystery part, 2 pins [chip_label=5V]  # not connected
  U3 = mystery part, 2 pins [chip_label=12V]
  U5 = mystery part, 2 pins [chip_label=?]
  Q5 = TRANSISTOR_NPN [package=to-92-ammo]
  R3 = Resistor [tolerance=±5% resistance=10k package=THT]
  Raspberry_Pi1 = Raspberry Pi B+
  R4 = Resistor [tolerance=±5% resistance=10k package=THT]
  R5 = Trimmer Potentiometer [maximum_resistance=10kΩ package=THT]
  U7 = RELAY [package=relay-jzc]  # not connected
  J1 = Screw terminal - 2 pins [package=THT]  # not connected
  U8 = RELAY [package=relay-jzc]  # not connected

nets:
  N1: LED1.red_anode, Composant1.D11/MOSI
  N2: LED1.green_anode, Composant1.D10
  GND: Composant1.GND, Q5.C, Raspberry_Pi1.GND
  N3: Composant1.D12/MISO, S1.1
  N4: Composant1.A5, Raspberry_Pi1.GPIO3
  N5: Composant1.A4, Raspberry_Pi1.GPIO2
  N6: Composant1.A1, R5.wiper
  N7: S1.2, R4.Pin_0
  N8: S1.4, R3.Pin_0
  N9: U3.pin2, U5.pin1
  N10: Q5.E, R3.Pin_1
  N11: Q5.B, Raspberry_Pi1.GPIO14

notes:
  Alim 5V
  Alim 12V
  Carte fille Ecran LCD
  I2C : shutdown ->
  volume ->
  ready <-
  Volume
  On/Off
  LED d'état
  Run
  Relie les masses
